# Fritzing sketch circuit (saved by Fritzing 0.9.6b)
breadboards: 1

parts:
  IC1 = PICAXE-28 [package=THT]
  Power_plug1 = Power plug
  PWM1 = PCA9685 16x12-bit PWM Breakout
  R1 = Resistor [tolerance=±5% power=0.25 resistance=10k package=THT]
  R2 = Resistor [tolerance=±5% power=0.25 resistance=10k package=THT]
  パーツ1 = HC-05 [part_number=HC-05 package="breakout board"]
  R3 = Resistor [tolerance=±5% power=0.25 resistance=2.2k package=THT]
  R4 = Resistor [tolerance=±5% power=0.25 resistance=1k package=THT]
  VCC1 = 4 x AAA Battery Mount

nets:
  GND: IC1.0V, Power_plug1.GND, PWM1.no_name_yet#501, PWM1.no_name_yet#701, パーツ1.GND, R3.Pin_1, VCC1.+
  N1: IC1.In_3, R2.Pin_1
  N2: IC1.In_4, R1.Pin_1
  N3: IC1.In_6, R4.Pin_0
  N4: IC1.In_7, パーツ1.TXD
  VCC: IC1.+V, Power_plug1.VCC, PWM1.no_name_yet#505, パーツ1.VCC
  N5: PWM1.no_name_yet#503, R2.Pin_0
  N6: PWM1.no_name_yet#504, R1.Pin_0
  N7: PWM1.no_name_yet#706, VCC1.-
  N8: パーツ1.RXD, R3.Pin_0, R4.Pin_1

custom parts:
  HC-05: A commonly available HC-05 Bluetooth breakout board.
